// Logisim project Trabalho1.circ as structural Verilog: 1 circuit, main circuit main
module main (
  input  reset,
  input  count_load,
  input  en_ULA,
  input  [1:0] ULA_sel,
  output out_5,
  output out_6,
  output out_7,
  output out_8,
  output out_9,
  output out_10,
  output out_11,
  output out_12,
  output out_13
);

  wire clock_out, comparator_1_eq, not_1_out, not_2_out;
  wire [3:0] ACC_q, adder_1_out, multiplexer_1_out, multiplier_1_out, PC_q, RDM_q, subtractor_1_out;
  wire [7:0] ram_1_data;
  wire [7:4] RDM_q_2;

  not not_1 (not_1_out, reset);
  Clock clock (.out(clock_out));
  Counter #(.width(4), .max('hf)) PC (
    .load(not_2_out), .D(RDM_q), .count(count_load), .Q(PC_q), .clk(clock_out), .clr(not_1_out));  // open: carry
  not not_2 (not_2_out, count_load);
  Adder #(.width(4)) adder_1 (.a(ACC_q), .b(RDM_q), .out(adder_1_out));  // open: cin, cout
  Subtractor #(.width(4)) subtractor_1 (.a(ACC_q), .b(RDM_q), .out(subtractor_1_out));  // open: bin, bout
  Multiplier #(.width(4)) multiplier_1 (.a(ACC_q), .b(RDM_q), .out(multiplier_1_out));  // open: cin, cout
  Multiplexer #(.select(2), .width(4), .enable("false")) multiplexer_1 (
    .in0(RDM_q), .in1(adder_1_out), .in2(subtractor_1_out), .in3(multiplier_1_out), .out(multiplexer_1_out),
    .sel(ULA_sel));
  RAM #(.addrWidth(4)) ram_1 (.addr(PC_q), .data(ram_1_data));  // open: sel, clk, ld, clr
  Comparator #(.width(4)) comparator_1 (.a(multiplexer_1_out), .b(4'b0000), .eq(comparator_1_eq));  // open: gt, lt
  Register RDM (.D(ram_1_data), .Q({RDM_q_2, RDM_q}), .clk(clock_out), .clr(not_1_out));  // open: en
  Register #(.width(1)) Z (.D(comparator_1_eq), .en(en_ULA), .Q(out_5), .clk(clock_out), .clr(not_1_out));
  Register #(.width(4)) ACC (.D(multiplexer_1_out), .en(en_ULA), .Q(ACC_q), .clk(clock_out), .clr(not_1_out));
  Register #(.width(1)) N (.D(multiplexer_1_out[3]), .en(en_ULA), .Q(out_13), .clk(clock_out), .clr(not_1_out));
  Decoder #(.select(4), .enable("false")) decoder_1 (
    .out0(out_6), .out1(out_7), .out2(out_8), .out3(out_9), .out4(out_10), .out5(out_11), .out6(out_12),
    .sel(RDM_q_2));  // open: out7, out8, out9, out10, out11, out12, out13, out14, out15

  // Notes on the sheet:
  //   LD - 0
  //   ADD - 1
  //   SUB - 2
  //   MUL - 3
  //   JMP - 4
  //   JZ - 5
  //   JN - 6
endmodule
